// Logisim project alu.circ as structural Verilog: 1 circuit, main circuit alu
module alu (
  input  [3:0] alu_op,
  input  alu_cin,
  input  [7:0] alu_a,
  input  [7:0] alu_b,
  output [7:0] alu_r,
  output alu_c,
  output alu_n,
  output alu_f,
  output alu_z,
  output alu_e,
  output alu_s
);

  wire alu_c_add;
  wire [7:0] alu_and, alu_or, alu_shl, alu_sr, alu_sum, alu_xor;

  arith8 arith8_1 (
    .arith8_one(alu_op[2]), .arith8_sub(alu_op[0]), .arith8_use_c(alu_op[1]), .arith8_cin(alu_cin),
    .arith8_c(alu_c_add), .arith8_a(alu_a), .arith8_b(alu_b), .arith8_s(alu_sum));
  logic8 logic8_1 (.logic8_a(alu_a), .logic8_b(alu_b), .logic8_and(alu_and), .logic8_or(alu_or), .logic8_xor(alu_xor));
  shift8 shift8_1 (
    .shift8_sel(alu_op[3]), .shift8_asr(alu_op[0]), .shift8_c_add(alu_c_add), .shift8_c(alu_c),
    .shift8_a(alu_a), .shift8_shl(alu_shl), .shift8_sr(alu_sr));
  rmux8 rmux8_1 (
    .rmux8_op(alu_op), .rmux8_sum(alu_sum), .rmux8_and(alu_and), .rmux8_or(alu_or), .rmux8_xor(alu_xor),
    .rmux8_a(alu_a), .rmux8_shl(alu_shl), .rmux8_sr(alu_sr), .rmux8_r(alu_r));
  flags8 flags8_1 (
    .flags8_n(alu_n), .flags8_f(alu_f), .flags8_z(alu_z), .flags8_e(alu_e), .flags8_s(alu_s),
    .flags8_r(alu_r), .flags8_c(alu_c_add));

  // Other names for the same wires on the sheet: alu_op_0 = alu_op[0]; alu_op_1 = alu_op[1]; alu_op_2 = alu_op[2];
  //   alu_op_3 = alu_op[3]
endmodule
