// Logisim project flags8.circ as structural Verilog: 1 circuit, main circuit flags8
module flags8 (
  input  [7:0] flags8_r,
  output flags8_n,
  output flags8_z
);

  wire U1_pin6, U1_pin8, U1_pin11, U1_pin12, U2_pin1, U2_pin2, U2_pin3, U2_pin4, U2_pin5, U2_pin13;

  _7427 U1 (
    .pin1(flags8_r[0]), .pin2(flags8_r[1]), .pin3(flags8_r[3]), .pin4(flags8_r[4]), .pin5(flags8_r[5]),
    .pin6(U1_pin6), .pin13(flags8_r[2]), .pin12(U1_pin12), .pin11(U1_pin11), .pin10(flags8_r[7]),
    .pin9(flags8_r[6]), .pin8(U1_pin8));
  _7411 U2 (
    .pin1(U2_pin1), .pin2(U2_pin2), .pin3(U2_pin3), .pin4(U2_pin4), .pin5(U2_pin5), .pin13(U2_pin13),
    .pin11(U1_pin8), .pin10(U1_pin6), .pin9(U1_pin12), .pin8(flags8_z));  // open: pin6, pin12

  assign flags8_n = flags8_r[7];
  // also tied to GND on the sheet: {U1_pin11, U2_pin13, U2_pin1, U2_pin2, U2_pin3, U2_pin4, U2_pin5}

  // Notes on the sheet:
  //   z: nor of r
  //   z: and
endmodule
